# Fritzing sketch Untitled Sketch (saved by Fritzing 0.9.9b)
breadboards: 1

parts:
  HC-SR04_Distance_sensor_1 = HC-SR04 Ultrasonic Distance Sensor
  HC-SR04_Distance_sensor_2 = HC-SR04 Ultrasonic Distance Sensor
  SPKR1 = Loudspeaker
  Part1 = Arduino Nano (Rev3.0) (ICSP)
  Part2 = Logic Level Converter
  Part3 = Adafruit MAX98357A I2S 3W Class D Amplifier [part_number="Adafruit #3006"]
  DC_Mot_Enc1 = DC Motor with two-phase hall-encoder [part_number=VT-E-G25A-06-177E]
  VCC1 = 4 x AAA Battery Mount
  DC_Mot_Enc2 = DC Motor with two-phase hall-encoder [part_number=VT-E-G25A-06-177E]
  Mod1 = Raspberry Pi 4B
  CAMERA1 = TTL Serial JPEG Camera
  J1 = Basic Servo
  J2 = Basic Servo

nets:
  N1: HC-SR04_Distance_sensor_1.VCC, Mod1.GPIO4
  N2: HC-SR04_Distance_sensor_1.TRIG, Mod1.GPIO3
  N3: HC-SR04_Distance_sensor_1.ECHO, Mod1.GPIO2
  GND: HC-SR04_Distance_sensor_1.GND, Part2.GND, Part3.GND, Mod1.GND, CAMERA1.GND, J1.gnd, J2.gnd
  VCC: HC-SR04_Distance_sensor_2.VCC, Part1.5V, Part2.HV, Part3.VIN, Part3.SD_MODE, DC_Mot_Enc1.pin2, DC_Mot_Enc2.pin2
  N4: HC-SR04_Distance_sensor_2.TRIG, Part1.A4
  N5: HC-SR04_Distance_sensor_2.ECHO, Part1.A5
  GND_2: HC-SR04_Distance_sensor_2.GND, Part1.GND, DC_Mot_Enc1.pin5, DC_Mot_Enc2.pin5
  N6: SPKR1.pin1, Part3.VO+
  N7: SPKR1.pin2, Part3.VO-
  N8: Part1.D1/TX, Part2.TX_HV
  N9: Part1.D0/RX, Part2.RX2_HV
  N10: Part1.D5, Part3.LRCLK
  N11: Part1.D6, Part3.BCLK
  N12: Part1.D7, DC_Mot_Enc2.pin4
  N13: Part1.D8, DC_Mot_Enc2.pin3
  N14: Part1.D9, DC_Mot_Enc1.pin4
  N15: Part1.D10, DC_Mot_Enc1.pin3
  5V: Part1.VIN, Mod1.5V, CAMERA1.5V
  N16: Part1.A3, Part3.DIN
  N17: Part2.RX2_LV, Mod1.GPIO15, CAMERA1.TX
  VCC_2: Part2.LV, Mod1.3V3, J1.vcc, J2.vcc
  N18: Part2.TX_LV, Mod1.GPIO14, CAMERA1.RX
  N19: DC_Mot_Enc1.pin1, VCC1.+, DC_Mot_Enc2.pin1
  N20: DC_Mot_Enc1.pin6, VCC1.-, DC_Mot_Enc2.pin6
  N21: Mod1.GPIO17, J1.pulse
  N22: Mod1.GPIO18, J2.pulse

custom parts:
  Adafruit MAX98357A I2S 3W Class D Amplifier: Listen to this good news - we now have an all in one digital audio amp breakout board that works incredibly well with the Raspberry Pi! If you're looking for an easy and low cost way to get you digital sound files bumpin' then the MAX08357 I2S Amp Breakout is for you. It takes standard I2S digital audio input and, not only decodes it into analog, but also amplifies it directly into a speaker.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
  TTL Serial JPEG Camera: TTL Serial JPEG Camera with NTSC Out
